# Fritzing sketch Esquema_bola (saved by Fritzing 0.9.2b)
breadboards: 1

parts:
  Parte1 = Arduino Nano (Rev3.0)
  Parte2 = Triple Axis Accelerometer Breakout - ADXL345
  8x8_LED_Modul_mit_MAX1 = 8x8 LED Modul mit MAX7219 [package=THT]

nets:
  GND: Parte1.GND, Parte2.GND, 8x8_LED_Modul_mit_MAX1.GND_Eingang
  N1: Parte1.D10, 8x8_LED_Modul_mit_MAX1.CS_Eingang
  N2: Parte1.D11/MOSI, 8x8_LED_Modul_mit_MAX1.CLK_Eingang
  N3: Parte1.D12/MISO, 8x8_LED_Modul_mit_MAX1.DIN_Eingang
  N4: Parte1.5V, 8x8_LED_Modul_mit_MAX1.VCC_Eingang
  N5: Parte1.A5, Parte2.SCL
  N6: Parte1.A4, Parte2.SDA
  3V3: Parte1.3V3, Parte2.VCC, Parte2.CS
